// Logisim project TallerLogica-Combinatorios.circ as structural Verilog: 12 circuits, main circuit ALU
module sumador_simple (
  input  a,
  input  b,
  output S,
  output Cout
);

  and and_1 (Cout, a, b);
  xor xor_1 (S, a, b);
endmodule

module sumador_completo (
  input  A,
  input  B,
  input  Cin,
  output S,
  output Cout
);

  wire sumador_simple_1_cout, sumador_simple_1_s, sumador_simple_2_cout;

  sumador_simple sumador_simple_1 (.a(B), .b(Cin), .S(sumador_simple_1_s), .Cout(sumador_simple_1_cout));
  sumador_simple sumador_simple_2 (.a(A), .b(sumador_simple_1_s), .S(S), .Cout(sumador_simple_2_cout));
  or or_1 (Cout, sumador_simple_2_cout, sumador_simple_1_cout);
endmodule

module sumador_4 (
  input  Cin,
  input  [3:0] A,
  input  [3:0] B,
  output [3:0] S,
  output Cout
);

  wire sumador_completo_1_cout, sumador_completo_2_cout, sumador_completo_3_cout;

  sumador_completo sumador_completo_1 (.A(A[0]), .B(B[0]), .Cin(Cin), .S(S[0]), .Cout(sumador_completo_1_cout));
  sumador_completo sumador_completo_2 (
    .A(A[1]), .B(B[1]), .Cin(sumador_completo_1_cout), .S(S[1]), .Cout(sumador_completo_2_cout));
  sumador_completo sumador_completo_3 (
    .A(A[2]), .B(B[2]), .Cin(sumador_completo_2_cout), .S(S[2]), .Cout(sumador_completo_3_cout));
  sumador_completo sumador_completo_4 (.A(A[3]), .B(B[3]), .Cin(sumador_completo_3_cout), .S(S[3]), .Cout(Cout));
  Hex_Digit_Display hex_digit_display_1 (.value(S));  // open: dp
endmodule

module comparador_cero (
  input  [3:0] A,
  output Z
);

  wire and_1_out, and_2_out, not_1_out, not_2_out, not_3_out, not_4_out;

  not not_1 (not_1_out, A[2]);
  not not_2 (not_2_out, A[3]);
  not not_3 (not_3_out, A[0]);
  not not_4 (not_4_out, A[1]);
  and and_1 (and_1_out, not_1_out, not_2_out);
  and and_2 (and_2_out, not_3_out, not_4_out);
  and and_3 (Z, and_2_out, and_1_out);
endmodule

module sumador_flags (
  input  Cin,
  input  [3:0] A,
  input  [3:0] B,
  output [3:0] S,
  output N,
  output Z,
  output V,
  output C
);

  wire sumador_completo_flags_1_coutanterior;

  xor xor_1 (V, C, sumador_completo_flags_1_coutanterior);
  sumador_completo_flags sumador_completo_flags_1 (
    .A(A), .B(B), .Cin(Cin), .Cout(C), .CoutAnterior(sumador_completo_flags_1_coutanterior), .S({N, S[2:0]}));
  Hex_Digit_Display hex_digit_display_1 (.value({N, S[2:0]}));  // open: dp
  comparador_cero comparador_cero_1 (.A({N, S[2:0]}), .Z(Z));

  assign S[3] = N;
endmodule

module incrementador_4 (
  input  [3:0] A,
  output [3:0] S,
  output out_3
);

  sumador_flags sumador_flags_1 (.A(4'b0001), .B(A), .Cin(1'b0), .S(S), .C(out_3));  // open: N, Z, V
  Hex_Digit_Display hex_digit_display_1 (.value(S));  // open: dp
endmodule

module inversor_4 (
  input  [3:0] A,
  input  INV,
  output [3:0] S
);

  wire not_1_out;
  wire [3:0] incrementador_4_1_s, xor_1_out;

  xor xor_1 (xor_1_out[0], A[0], INV);
  xor xor_2 (xor_1_out[1], A[1], INV);
  xor xor_3 (xor_1_out[2], A[2], INV);
  xor xor_4 (xor_1_out[3], A[3], INV);
  incrementador_4 incrementador_4_1 (.A(xor_1_out), .S(incrementador_4_1_s));  // open: out_3
  not not_1 (not_1_out, INV);
  assign S = INV ? incrementador_4_1_s : 4'bz;  // Controlled_Buffer controlled_buffer_1
  assign S = not_1_out ? xor_1_out : 4'bz;  // Controlled_Buffer controlled_buffer_2
  Hex_Digit_Display hex_digit_display_1 (.value(S));  // open: dp
endmodule

module ALU (
  input  [3:0] A,
  input  [3:0] B,
  input  [1:0] OP,
  output N,
  output Z,
  output V,
  output C,
  output [3:0] S
);

  wire and_2_out, not_1_out, not_2_out, sumador_flags_1_c, sumador_flags_1_v, xor_1_out;
  wire [3:0] and_1_out, inversor_4_1_s, or_1_out, sumador_flags_1_s;

  inversor_4 inversor_4_1 (.A(B), .INV(and_2_out), .S(inversor_4_1_s));
  assign and_1_out = A & B;  // AND_Gate and_1, 4 bits wide
  assign or_1_out = A | B;  // OR_Gate or_1, 4 bits wide
  xor xor_1 (xor_1_out, OP[0], OP[1]);
  and and_2 (and_2_out, xor_1_out, not_1_out);
  not not_1 (not_1_out, OP[1]);
  sumador_flags sumador_flags_1 (
    .A(A), .B(inversor_4_1_s), .Cin(1'b0), .S(sumador_flags_1_s), .V(sumador_flags_1_v), .C(sumador_flags_1_c));  // open: N, Z
  not not_2 (not_2_out, sumador_flags_1_c);
  Multiplexer #(.select(2), .width(4), .enable("false")) multiplexer_1 (
    .in0(sumador_flags_1_s), .in1(sumador_flags_1_s), .in2(and_1_out), .in3(or_1_out), .out({N, S[2:0]}),
    .sel(OP));
  Multiplexer #(.select(2), .enable("false")) multiplexer_2 (
    .in0(sumador_flags_1_v), .in1(sumador_flags_1_v), .in2(1'b0), .in3(1'b0), .out(V), .sel(OP));
  Multiplexer #(.select(2), .enable("false")) multiplexer_3 (
    .in0(sumador_flags_1_c), .in1(not_2_out), .in2(1'b0), .in3(1'b0), .out(C), .sel(OP));
  comparador_cero comparador_cero_1 (.A({N, S[2:0]}), .Z(Z));
  Hex_Digit_Display hex_digit_display_1 (.value({N, S[2:0]}));  // open: dp

  assign S[3] = N;
endmodule

module verificador (
  output [3:0] a,
  output [3:0] b,
  output [1:0] Op,
  output N,
  output Z,
  output V,
  output C,
  output [3:0] Res,
  output halt
);

  wire clock_1_out;

  Clock clock_1 (.out(clock_1_out));
  Counter #(.width(10), .max('h3ff)) counter_1 (
    .Q({Op, b, a}), .carry(halt), .clk(clock_1_out));  // open: load, D, count, clr
  ALU alu_1 (.A(a), .B(b), .OP(Op), .N(N), .Z(Z), .V(V), .C(C), .S(Res));
endmodule

module sumador_completo_flags (
  input  Cin,
  input  [3:0] A,
  input  [3:0] B,
  output [3:0] S,
  output Cout,
  output CoutAnterior
);

  wire sumador_completo_1_cout, sumador_completo_2_cout;

  sumador_completo sumador_completo_1 (.A(A[0]), .B(B[0]), .Cin(Cin), .S(S[0]), .Cout(sumador_completo_1_cout));
  sumador_completo sumador_completo_2 (
    .A(A[1]), .B(B[1]), .Cin(sumador_completo_1_cout), .S(S[1]), .Cout(sumador_completo_2_cout));
  sumador_completo sumador_completo_3 (
    .A(A[2]), .B(B[2]), .Cin(sumador_completo_2_cout), .S(S[2]), .Cout(CoutAnterior));
  sumador_completo sumador_completo_4 (.A(A[3]), .B(B[3]), .Cin(CoutAnterior), .S(S[3]), .Cout(Cout));
  Hex_Digit_Display hex_digit_display_1 (.value(S));  // open: dp
endmodule

module demul (
  input  in_1,
  input  in_2
);

  wire and_1_out, not_1_out, not_2_out;

  not not_1 (not_1_out, in_2);
  not not_2 (not_2_out, in_1);
  and and_1 (and_1_out, not_1_out, not_2_out);
  // AND_Gate and_2 is placed but not wired
  // AND_Gate and_3 is placed but not wired
  // AND_Gate and_4 is placed but not wired
  // AND_Gate and_5 has open pins: in0=and_1_out, out=open
endmodule

module OR4 (
  input  [3:0] in_1,
  input  [3:0] in_2,
  output [3:0] out_3
);

  or or_1 (out_3[0], in_1[0], in_2[0]);
  or or_2 (out_3[1], in_1[1], in_2[1]);
  or or_3 (out_3[2], in_1[2], in_2[2]);
  or or_4 (out_3[3], in_1[3], in_2[3]);
endmodule
